// Digital circuit alu.dig as structural Verilog
module alu (
  input  [7:0] ALU_0,
  input  [7:0] ALU_1,
  input  [4:0] OPC,
  input  C_i,
  input  ALU_r,
  output [7:0] D_o,
  output Z_o,
  output C_o
);

  wire ADD_c_o, and_1_out, decoder_1_out_1, decoder_1_out_2, decoder_1_out_3, decoder_1_out_8,
       decoder_1_out_9, not_2_out, or_1_out;
  wire [0:0] or_2_out;
  wire [7:0] ADD_s, and_2_out, multiplexer_1_out, multiplexer_2_out, multiplexer_3_out, not_1_out, or_3_out,
       xor_1_out;

  Decoder #(.Selector_Bits(4)) decoder_1 (
    .sel(OPC[3:0]), .out_1(decoder_1_out_1), .out_2(decoder_1_out_2), .out_3(decoder_1_out_3),
    .out_8(decoder_1_out_8), .out_9(decoder_1_out_9));  // open: out_0, out_4, out_5, out_6, out_7, out_10, out_11, out_12, out_13, out_14, out_15
  Multiplexer #(.Bits(8)) multiplexer_1 (
    .sel(decoder_1_out_3), .in_0(ALU_1), .in_1({8{1'b1}}), .out(multiplexer_1_out));
  or or_1 (or_1_out, decoder_1_out_1, decoder_1_out_8, decoder_1_out_9);
  Multiplexer #(.Bits(8)) multiplexer_2 (
    .sel(decoder_1_out_2), .in_0(multiplexer_1_out), .in_1({8{1'b0}}), .out(multiplexer_2_out));
  and and_1 (and_1_out, C_i, or_1_out);
  or or_2 (or_2_out[0], and_1_out, decoder_1_out_2);
  Add #(.Bits(8)) ADD (.a(ALU_0), .b(multiplexer_2_out), .c_i(or_2_out[0]), .s(ADD_s), .c_o(ADD_c_o));
  assign and_2_out = ALU_0 & multiplexer_2_out;  // And and_2, 8 bits wide
  assign or_3_out = ALU_0 | multiplexer_2_out;  // Or or_3, 8 bits wide
  assign xor_1_out = ALU_0 ^ multiplexer_2_out;  // XOr xor_1, 8 bits wide
  assign not_1_out = ~ALU_0;  // Not not_1, 8 bits wide
  not not_2 (not_2_out, ADD_c_o);
  Multiplexer #(.Selector_Bits(4), .Bits(8)) multiplexer_3 (
    .sel(OPC[3:0]), .in_0(ADD_s), .in_1(ADD_s), .in_2(ADD_s), .in_3(ADD_s), .in_4(and_2_out),
    .in_5(or_3_out), .in_6(xor_1_out), .in_7(not_1_out), .in_8({ALU_0[6:0], or_2_out[0]}),
    .in_9({or_2_out[0], ALU_0[7:1]}), .in_10({8{1'b0}}), .in_11({8{1'b0}}), .in_12({8{1'b0}}),
    .in_13({8{1'b0}}), .in_14({8{1'b0}}), .in_15({8{1'b0}}), .out(multiplexer_3_out));
  Multiplexer #(.Selector_Bits(4)) multiplexer_4 (
    .sel(OPC[3:0]), .in_0(ADD_c_o), .in_1(ADD_c_o), .in_2(ADD_c_o), .in_3(not_2_out), .in_4(1'b0),
    .in_5(1'b0), .in_6(1'b0), .in_7(1'b0), .in_8(ALU_0[7]), .in_9(ALU_0[0]), .in_10(1'b0), .in_11(1'b0),
    .in_12(1'b0), .in_13(1'b0), .in_14(1'b0), .in_15(1'b0), .out(C_o));
  assign D_o = ALU_r ? multiplexer_3_out : 8'bz;  // Driver driver_1
  Comparator #(.Bits(8)) comparator_1 (.a(multiplexer_3_out), .b({8{1'b0}}), .eq(Z_o));  // open: gt, lt

  // Other names for the same wires on the sheet: sel[3:0] = OPC[3:0]

  // Notes on the sheet:
  //   C_i: Carry input
  //   D_o: Data output
  //   Z_o: Zero detect output
  //   C_o: Carry output
  //   ROLC
  //   RORC
endmodule
