// Digital circuit control.dig as structural Verilog
module control (
  input  CLK,
  input  run,
  input  Z,
  input  C,
  input  [4:0] OPC,
  input  auto,
  output [1:0] cycle_o,
  output [19:0] control_o,
  output HLT,
  output PC_inc,
  output PC_r,
  output PC_w,
  output RAM_r,
  output RAM_w,
  output IRH_w,
  output IRL_w,
  output [2:0] A_mode,
  output Rs_src,
  output Rd_w,
  output Rs_r,
  output SP_cnt,
  output SP_push,
  output ALU_r,
  output C_ctrl,
  output C_src
);

  wire not_1_out, not_2_out;
  wire [8:8] driver_1_out;

  not not_1 (not_1_out, CLK);
  not not_2 (not_2_out, run);
  Counter #(.Bits(2)) Cycle (.en(run), .C(not_1_out), .clr(not_2_out), .out(cycle_o));  // open: ovf
  ROM #(.AddrBits(9), .Bits(20)) Control (.A({OPC, Z, C, cycle_o}), .sel(1'b1), .D(control_o));
  assign {HLT, PC_inc, PC_r, PC_w, RAM_r, RAM_w, IRH_w, IRL_w, A_mode, driver_1_out[8], Rs_src, Rd_w, Rs_r, SP_cnt, SP_push, ALU_r, C_ctrl, C_src} = auto ? control_o : 20'bz;  // Driver driver_1

  // Notes on the sheet:
  //   SP_cnt: Increment or decrement the stack pointer if this is high 
  //   on the next clock rising edge
  //   auto: Set to 1 to use the program controller.
  //   0 is manual
  //   SP_push: Direction that stack pointer moves when SP_cnt is high
  //   1 = push on to stack
  //   0 = pull from stack
  //   C_ctrl: Force the Carry bit to this state
  //   C_src: The source that the Status register must use 
  //   for the Carry bit.
  //   0 = ALU
  //   1 = Controller
  //   contents of Control (hex, n*v repeats v):
  //   1a800,1a400,20000,0,1a800,1a400,20000,0,1a800,1a400,20000,0,1a800,1a400,20000,0,1a800,
  //   1a400,210,0,1a800,1a400,210,0,1a800,1a400,210,0,1a800,1a400,210,0,1a800,1a400,2110,
  //   0,1a800,1a400,2110,0,1a800,1a400,2110,0,1a800,1a400,2110,0,1a800,1a400,2050,0,1a800,
  //   1a400,2050,0,1a800,1a400,2050,0,1a800,1a400,2050,0,1a800,1a400,1108,0,1a800,1a400,
  //   1108,0,1a800,1a400,1108,0,1a800,1a400,1108,0,1a800,1a400,1048,0,1a800,1a400,1048,
  //   0,1a800,1a400,1048,0,1a800,1a400,1048,0,1a800,1a400,38,0,1a800,1a400,38,0,1a800,1a400,
  //   38,0,1a800,1a400,38,0,1a800,1a400,4080,0,1a800,1a400,4080,0,1a800,1a400,4080,0,1a800,
  //   1a400,4080,0,1a800,1a400,0,0,1a800,1a400,4080,0,1a800,1a400,0,0,1a800,1a400,4080,
  //   0,1a800,1a400,4080,0,1a800,1a400,0,0,1a800,1a400,4080,0,1a800,1a400,0,0,1a800,1a400,
  //   0,0,1a800,1a400,0,0,1a800,1a400,4080,0,1a800,1a400,4080,0,1a800,1a400,4080,0,1a800,
  //   1a400,4080,0,1a800,1a400,0,0,1a800,1a400,0,0,1a800,1a400,8002,4080,1a800,1a400,8002,
  //   4080,1a800,1a400,8002,4080,1a800,1a400,8002,4080,1a800,1a400,4004,0,1a800,1a400,4004,
  //   0,1a800,1a400,4004,0,1a800,1a400,4004,0,1a800,1a400,0,0,1a800,1a400,0,0,1a800,1a400,
  //   0,0,1a800,1a400,0,0,1a800,1a400,0,0,1a800,1a400,0,0,1a800,1a400,0,0,1a800,1a400,0,
  //   0,1a800,1a400,11,0,1a800,1a400,11,0,1a800,1a400,11,0,1a800,1a400,11,0,1a800,1a400,
  //   11,0,1a800,1a400,11,0,1a800,1a400,11,0,1a800,1a400,11,0,1a800,1a400,11,0,1a800,1a400,
  //   11,0,1a800,1a400,11,0,1a800,1a400,11,0,1a800,1a400,11,0,1a800,1a400,11,0,1a800,1a400,
  //   11,0,1a800,1a400,11,0,1a800,1a400,11,0,1a800,1a400,11,0,1a800,1a400,11,0,1a800,1a400,
  //   11,0,1a800,1a400,11,0,1a800,1a400,11,0,1a800,1a400,11,0,1a800,1a400,11,0,1a800,1a400,
  //   11,0,1a800,1a400,11,0,1a800,1a400,11,0,1a800,1a400,11,0,1a800,1a400,11,0,1a800,1a400,
  //   11,0,1a800,1a400,11,0,1a800,1a400,11,0,1a800,1a400,11,0,1a800,1a400,11,0,1a800,1a400,
  //   11,0,1a800,1a400,11,0,1a800,1a400,11,0,1a800,1a400,11,0,1a800,1a400,11,0,1a800,1a400,
  //   11,0,1a800,1a400,0,0,1a800,1a400,0,0,1a800,1a400,0,0,1a800,1a400,0,0,1a800,1a400,
  //   0,0,1a800,1a400,0,0,1a800,1a400,0,0,1a800,1a400,0,0,1a800,1a400,0,0,1a800,1a400,0,
  //   0,1a800,1a400,0,0,1a800,1a400,0,0,1a800,1a400,0,0,1a800,1a400,0,0,1a800,1a400,0,0,
  //   1a800,1a400,0,0,1a800,1a400,0,0,1a800,1a400,0,0,1a800,1a400,0,0,1a800,1a400,0,0,1a800,
  //   1a400,0,0,1a800,1a400,0,0,1a800,1a400,0,0,1a800,1a400
endmodule
