// Digital circuit cpu.dig as structural Verilog
module cpu (
  input  Clock,
  input  PC_inc,
  input  PC_r,
  input  PC_w,
  input  IRH_w,
  input  IRL_w,
  input  Rs_src,
  input  Rd_w,
  input  Rs_r,
  input  SP_cnt,
  input  SP_push,
  input  RAM_r,
  input  RAM_w,
  input  ALU_r,
  input  HLT,
  input  auto,
  input  run,
  input  C_ctrl,
  input  C_src,
  input  Clock_2,
  input  manual,
  input  [15:0] BRKPT,
  input  [7:0] SPPS,
  input  A,
  input  [2:0] A_mode,
  output [1:0] Cycle_out,
  output [19:0] control_out,
  output [4:0] Opcode,
  output [15:0] PC,
  output [7:0] out_26,
  output [7:0] out_27,
  output [7:0] out_28,
  output [7:0] out_29,
  output [7:0] out_30
);

  wire alu_1_c_o, alu_1_z_o, ALU_r_t, C_ctrl_t, C_src_t, CLK, comparator_1_eq, HLT_t, INH, instruction_1_nst,
       IRH_w_t, IRL_w_t, multiplexer_1_out, or_1_out, PC_inc_t, PC_r_t, PC_w_t, RAM_r_t, RAM_w_t, Rd_w_t,
       Rs_r_t, Rs_src_t, run_t, SP_cnt_t, SP_push_t, status_1_c_o, status_1_z_o;
  wire [2:0] A_mode_t, instruction_1_r_d, instruction_1_r_s0, instruction_1_r_s1;
  wire [7:0] instruction_1_opr8, ramsingleport_1_d, registers_1_alu_0, registers_1_alu_1, registers_1_page,
       registers_1_sp, registers_1_x;
  wire [10:0] instruction_1_opr11;
  wire [11:11] driverinvsel_1_out;
  wire [15:0] pc_1_a_out;

  assign {C_src_t, C_ctrl_t, ALU_r_t, SP_push_t, SP_cnt_t, Rs_r_t, Rd_w_t, Rs_src_t, driverinvsel_1_out[11], A_mode_t[0], A_mode_t[1], A_mode_t[2], IRL_w_t, IRH_w_t, RAM_w_t, RAM_r_t, PC_w_t, PC_r_t, PC_inc_t, HLT_t} = ~auto ? {C_src, C_ctrl, ALU_r, SP_push, SP_cnt, Rs_r, Rd_w, Rs_src, A, A_mode[0], A_mode[1], A_mode[2], IRL_w, IRH_w, RAM_w, RAM_r, PC_w, PC_r, PC_inc, HLT} : 20'bz;  // DriverInvSel driverinvsel_1
  pc pc_1 (
    .A_in(pc_1_a_out), .PC_inc(PC_inc_t), .CLK(CLK), .PC_r(PC_r_t), .PC_w(PC_w_t), .run(run_t),
    .A_out(pc_1_a_out), .PC(PC));
  Comparator #(.Bits(16)) comparator_1 (.a(PC), .b(BRKPT), .eq(comparator_1_eq));  // open: gt, lt
  RAMSinglePort #(.AddrBits(16), .isProgramMemory("true"), .Bits(8)) ramsingleport_1 (
    .A(pc_1_a_out), .str(RAM_w_t), .C(CLK), .ld(RAM_r_t), .D(ramsingleport_1_d));
  Multiplexer multiplexer_1 (.sel(manual), .in_0(Clock), .in_1(Clock_2), .out(multiplexer_1_out));
  or or_1 (or_1_out, comparator_1_eq, HLT_t);
  Break #(.Cycles(10000)) BRK (.brk(or_1_out));
  and and_1 (CLK, multiplexer_1_out, ~HLT_t);  // And
  instruction instruction_1 (
    .D_in(ramsingleport_1_d), .CLK(CLK), .IRH_w(IRH_w_t), .IRL_w(IRL_w_t), .Rs_src(Rs_src_t), .INH(INH),
    .R_d(instruction_1_r_d), .R_S0(instruction_1_r_s0), .R_S1(instruction_1_r_s1), .nSt(instruction_1_nst),
    .OPC(Opcode), .opr11(instruction_1_opr11), .opr8(instruction_1_opr8));
  D_FF d_ff_1 (.D(run), .C(~CLK), .Q(run_t));  // open: nQ
  registers registers_1 (
    .D_in(ramsingleport_1_d), .CLK(CLK), .R_d(instruction_1_r_d), .Rd_w(Rd_w_t), .R_S0(instruction_1_r_s0),
    .R_S1(instruction_1_r_s1), .Rs_r(Rs_r_t), .CMP(instruction_1_nst), .SP_cnt(SP_cnt_t),
    .SP_push(SP_push_t), .D_out(ramsingleport_1_d), .ALU_0(registers_1_alu_0), .ALU_1(registers_1_alu_1),
    .A(out_26), .B(out_27), .C(out_28), .D(out_29), .E(out_30), .PAGE(registers_1_page), .X(registers_1_x),
    .SP(registers_1_sp));
  alu alu_1 (
    .ALU_0(registers_1_alu_0), .ALU_1(registers_1_alu_1), .OPC(Opcode), .C_i(status_1_c_o), .ALU_r(ALU_r_t),
    .D_o(ramsingleport_1_d), .Z_o(alu_1_z_o), .C_o(alu_1_c_o));
  addressing addressing_1 (
    .PAGE(registers_1_page), .X(registers_1_x), .SP(registers_1_sp), .SPPS(SPPS),
    .opr11(instruction_1_opr11), .opr8(instruction_1_opr8), .PC(PC), .A_mode(A_mode_t),
    .D_out(ramsingleport_1_d), .A_out(pc_1_a_out), .INH(INH));
  status status_1 (
    .Z_alu(alu_1_z_o), .C_alu(alu_1_c_o), .ZC_w(ALU_r_t), .CLK(CLK), .C_ctrl(C_ctrl_t), .C_src(C_src_t),
    .Z_o(status_1_z_o), .C_o(status_1_c_o));
  // control control_1: pin names not known; wires that end beside it: pc_1_a_out, ramsingleport_1_d, CLK, run_t, status_1_z_o, status_1_c_o, Opcode, auto, Cycle_out, control_out, HLT_t, PC_inc_t, PC_r_t, PC_w_t, RAM_r_t, RAM_w_t, IRH_w_t, IRL_w_t, A_mode_t, Rs_src_t, Rd_w_t, Rs_r_t, SP_cnt_t, SP_push_t, ALU_r_t, C_ctrl_t, C_src_t

  // Notes on the sheet:
  //   Clock: Hz: 2
  //   Rd_w: Write to destination register
  //   Rs_r: Read from source register
  //   auto: Switch CPU control to auto (use controller)
  //   or control manually, default 1
  //   SPPS: Stack pointer page select
endmodule
