// Digital circuit pc.dig as structural Verilog
module pc (
  input  PC_inc,
  input  CLK,
  input  PC_r,
  input  PC_w,
  input  [15:0] A_in,
  input  run,
  output [15:0] A_out,
  output [15:0] PC
);

  wire not_1_out;

  not not_1 (not_1_out, run);
  CounterPreset #(.Bits(16)) u_PC (
    .en(PC_inc), .C(CLK), .dir(1'b0), .in(A_in), .ld(PC_w), .clr(not_1_out), .out(PC));  // open: ovf
  assign A_out = PC_r ? PC : 16'bz;  // Driver driver_1

  // Notes on the sheet:
  //   CLK: Hz: 5
endmodule
