// Digital circuit registers.dig as structural Verilog
module registers (
  input  [15:0] A_in,
  input  [7:0] D_in,
  input  CLK,
  input  [2:0] R_d,
  input  Rd_w,
  input  nSt,
  input  [2:0] R_S0,
  input  Rs_r,
  input  [2:0] R_S1,
  input  DIR8_sel,
  input  IND_sel,
  input  SPC_r,
  input  SPC_w,
  output [15:0] A_out,
  output [7:0] D_out,
  output [7:0] ALU_0,
  output [7:0] ALU_1,
  output [7:0] A,
  output [7:0] B,
  output [7:0] C,
  output [7:0] D,
  output [7:0] PAGE,
  output [7:0] X,
  output [7:0] SPCH,
  output [7:0] SPCL
);

  wire and_1_out, demultiplexer_1_out_0, demultiplexer_1_out_1, demultiplexer_1_out_2, demultiplexer_1_out_3,
       demultiplexer_1_out_4, demultiplexer_1_out_5, demultiplexer_1_out_6, demultiplexer_1_out_7, or_1_out,
       or_2_out, or_3_out;
  wire [7:0] multiplexer_1_out, multiplexer_2_out, multiplexer_5_out;

  and and_1 (and_1_out, Rd_w, ~nSt);  // And
  Demultiplexer #(.Selector_Bits(3)) demultiplexer_1 (
    .sel(R_d), .in(and_1_out), .out_0(demultiplexer_1_out_0), .out_1(demultiplexer_1_out_1),
    .out_2(demultiplexer_1_out_2), .out_3(demultiplexer_1_out_3), .out_4(demultiplexer_1_out_4),
    .out_5(demultiplexer_1_out_5), .out_6(demultiplexer_1_out_6), .out_7(demultiplexer_1_out_7));
  Multiplexer #(.Bits(8)) multiplexer_1 (.sel(SPC_w), .in_0(D_in), .in_1(A_in[15:8]), .out(multiplexer_1_out));
  Multiplexer #(.Bits(8)) multiplexer_2 (.sel(SPC_w), .in_0(D_in), .in_1(A_in[7:0]), .out(multiplexer_2_out));
  or or_1 (or_1_out, demultiplexer_1_out_6, SPC_w);
  or or_2 (or_2_out, SPC_w, demultiplexer_1_out_7);
  Register #(.Bits(8)) u_A (.D(D_in), .C(CLK), .en(demultiplexer_1_out_0), .Q(A));
  Register #(.Bits(8)) u_B (.D(D_in), .C(CLK), .en(demultiplexer_1_out_1), .Q(B));
  Register #(.Bits(8)) u_C (.D(D_in), .C(CLK), .en(demultiplexer_1_out_2), .Q(C));
  Register #(.Bits(8)) u_D (.D(D_in), .C(CLK), .en(demultiplexer_1_out_3), .Q(D));
  Register #(.Bits(8)) u_PAGE (.D(D_in), .C(CLK), .en(demultiplexer_1_out_4), .Q(PAGE));
  Register #(.Bits(8)) u_X (.D(D_in), .C(CLK), .en(demultiplexer_1_out_5), .Q(X));
  Register #(.Bits(8)) u_SPCH (.D(multiplexer_1_out), .C(CLK), .en(or_1_out), .Q(SPCH));
  Register #(.Bits(8)) u_SPCL (.D(multiplexer_2_out), .C(CLK), .en(or_2_out), .Q(SPCL));
  assign A_out[7:0] = IND_sel ? X : 8'bz;  // Driver driver_1
  or or_3 (or_3_out, IND_sel, DIR8_sel);
  Multiplexer #(.Selector_Bits(3), .Bits(8)) multiplexer_3 (
    .sel(R_S1), .in_0(A), .in_1(B), .in_2(C), .in_3(D), .in_4(PAGE), .in_5(X), .in_6(SPCH), .in_7(SPCL),
    .out(ALU_1));
  Multiplexer #(.Selector_Bits(3), .Bits(8)) multiplexer_4 (
    .sel(R_S0), .in_0(A), .in_1(B), .in_2(C), .in_3(D), .in_4(PAGE), .in_5(X), .in_6(SPCH), .in_7(SPCL),
    .out(ALU_0));
  Multiplexer #(.Selector_Bits(3), .Bits(8)) multiplexer_5 (
    .sel(R_S0), .in_0(A), .in_1(B), .in_2(C), .in_3(D), .in_4(PAGE), .in_5(X), .in_6(SPCH), .in_7(SPCL),
    .out(multiplexer_5_out));
  assign A_out[15:8] = or_3_out ? PAGE : 8'bz;  // Driver driver_2
  assign A_out = SPC_r ? {SPCH, SPCL} : 16'bz;  // Driver driver_3
  assign D_out = Rs_r ? multiplexer_5_out : 8'bz;  // Driver driver_4

  // Other names for the same wires on the sheet: D_t[7:0] = D_in

  // Notes on the sheet:
  //   A_in: Address bus input
  //   D_in: Data bus input
  //   R_d: Destination register selector.
  //   Write from data bus in to register.
  //   A_out: Address bus output
  //   Rd_w: Write enable for the register selected by Rd
  //   D_out: Data bus output
  //   nSt: Dont write to the register when this bit is high
  //   R_S0: Register to read from. Use RS0 as the source.
  //   Rs_r: Read enable selected by R_S0
  //   R_S1: Register to read from, gated on to the 2nd input of the ALU
  //   DIR8_sel: Direct addressing mode
  //   IND_sel: Indirect addressing mode
  //   SPC_r: Shadow Program Counter read.
  //   Read contents of SPCH and SPCL on to the address bus.
  //   Should be copied in to the PC (from Address bus.)
  //   SPC_w: Shadow Program Counter write enable.
  //   Write the address bus in to the SPCH and SPCL bytes.
  //   PC should output its bytes on to the address bus.
endmodule
