// Digital circuit status.dig as structural Verilog
module status (
  input  Z_i,
  input  C_i,
  input  en,
  input  CLK,
  output Z_o,
  output C_o
);

  Register Zero (.D(Z_i), .C(CLK), .en(en), .Q(Z_o));
  Register Carry (.D(C_i), .C(CLK), .en(en), .Q(C_o));
endmodule
